// Logisim project Logisim Projetos Circuitos.circ as structural Verilog: 1 circuit, main circuit main
module main (
  input  A,
  input  in_2,
  input  Vem_1,
  output S,
  output Vai_1
);

  wire and_1_out, and_2_out, or_1_out, xor_1_out;

  xor xor_1 (xor_1_out, A, in_2);
  or or_1 (or_1_out, in_2, Vem_1);
  xor xor_2 (S, xor_1_out, Vem_1);
  and and_1 (and_1_out, or_1_out, A);
  and and_2 (and_2_out, in_2, Vem_1);
  or or_2 (Vai_1, and_1_out, and_2_out);
endmodule
